# Fritzing sketch Untitled Sketch 2 (saved by Fritzing 0.9.3b)
breadboards: 1

parts:
  OLED1 = OLED 128x64 I2C Monochrome Display
  M1 = DOIT Esp32 DevKit v1 (30 pins long, 11 pins width) [part_number=ESP32S-PIN30]
  VALVE1 = Plastic Solenoid Valve
  VCC1 = Battery
  Composant1 = Jtron 1 Channel Optoisolated Relay Module [package=relay]

nets:
  GND: OLED1.GND, M1.GND, Composant1.GND
  VDD: OLED1.VDD, M1.3V3, Composant1.VCC
  N1: OLED1.SCK, M1.D22
  N2: OLED1.SDA, M1.D21
  N3: M1.D4, Composant1.IN1
  N4: VALVE1.no_name_yet#1, Composant1.MAIN
  N5: VALVE1.no_name_yet#2, VCC1.-
  N6: VCC1.+, Composant1.NO

notes:
  Serrure électrique
  Afficheur OLED SSD1306 I2C
  Module relais 3.3V
  ESP32 DevKit V1
  Alimentation 12 V

custom parts:
  DOIT Esp32 DevKit v1 (30 pins long, 11 pins width): The DOIT Esp32 DevKit v1 is one of the development board created by DOIT to evaluate the ESP-WROOM-32 module. It is based on the ESP32 microcontroller that boasts Wifi, Bluetooth, Ethernet and Low Power support all in a single chip. (vanepp) made breadboard work, adjusted pin numbering and labels and reduced size of schematic and cleaned up pcb. This chip is 30pins long (2 x15) and 11 pins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
